// Logisim project 2107038_ALU.circ as structural Verilog
module _2107038_ALU (
  input  [1:0] CONTROL,
  input  [18:0] A,
  input  [18:0] B,
  output [18:0] RESULT,
  output CARRY,
  output NEGATIVE,
  output OVERFLOW,
  output ZERO
);

  wire [18:0] add_sub_circuit_1_s, n19_bit_and_1_result, n19_bit_or_1_result;

  _19_bit_AND u_19_bit_and_1 (.A(A), .B(B), .Result(n19_bit_and_1_result));
  _19_bit_OR u_19_bit_or_1 (.A(A), .B(B), .Result(n19_bit_or_1_result));
  Add_Sub_circuit add_sub_circuit_1 (
    .A(A), .B(B), .SUB(CONTROL[0]), .S(add_sub_circuit_1_s), .Co(CARRY), .Overflow(OVERFLOW));
  Multiplexer #(.select(2), .width(19), .enable("false")) multiplexer_1 (
    .in0(n19_bit_and_1_result), .in1(n19_bit_or_1_result), .in2(add_sub_circuit_1_s),
    .in3(add_sub_circuit_1_s), .out(RESULT), .sel(CONTROL));
  _18th_bit_out u_18th_bit_out_1 (.in_1(RESULT), .out_2(NEGATIVE));
  _19_bit_Reduce_NOR u_19_bit_reduce_nor_1 (.in_1(RESULT), .out_2(ZERO));

  // Notes on the sheet:
  //   2107038
  //   ALU
  //   00 - AND
  //   01 - OR
  //   10 - ADD
  //   11 - SUB
endmodule

module Full_Adder (
  input  in_1,
  input  in_2,
  input  in_3,
  output out_4,
  output out_5
);

  wire and_1_out, and_2_out, xor_1_out;

  xor xor_1 (xor_1_out, in_2, in_3);
  and and_1 (and_1_out, in_3, in_2);
  and and_2 (and_2_out, xor_1_out, in_1);
  or or_1 (out_5, and_1_out, and_2_out);
  xor xor_2 (out_4, in_1, xor_1_out);
endmodule

module _6_bit_Full_Adder (
  input  in_1,
  input  in_2,
  input  in_3,
  input  in_4,
  input  in_5,
  input  in_6,
  input  in_7,
  input  in_8,
  input  in_9,
  input  in_10,
  input  in_11,
  input  in_12,
  input  in_13,
  output out_14,
  output out_15,
  output out_16,
  output out_17,
  output out_18,
  output out_19,
  output out_20
);

  wire full_adder_1_out_5, full_adder_2_out_5, full_adder_3_out_5, full_adder_4_out_5, full_adder_5_out_5;

  Full_Adder full_adder_1 (.in_1(in_1), .in_2(in_2), .out_4(out_14), .in_3(in_8), .out_5(full_adder_1_out_5));
  Full_Adder full_adder_2 (
    .in_1(full_adder_1_out_5), .in_2(in_3), .out_4(out_15), .in_3(in_9), .out_5(full_adder_2_out_5));
  Full_Adder full_adder_3 (
    .in_1(full_adder_2_out_5), .in_2(in_4), .out_4(out_16), .in_3(in_10), .out_5(full_adder_3_out_5));
  Full_Adder full_adder_4 (
    .in_1(full_adder_3_out_5), .in_2(in_5), .out_4(out_17), .in_3(in_11), .out_5(full_adder_4_out_5));
  Full_Adder full_adder_5 (
    .in_1(full_adder_4_out_5), .in_2(in_6), .out_4(out_18), .in_3(in_12), .out_5(full_adder_5_out_5));
  Full_Adder full_adder_6 (.in_1(full_adder_5_out_5), .in_2(in_7), .out_4(out_19), .in_3(in_13), .out_5(out_20));
endmodule

module _19_bit_Full_Adder (
  input  in_1,
  input  [18:0] in_2,
  input  [18:0] in_3,
  output [18:0] out_4,
  output out_5
);

  wire n6_bit_full_adder_1_out_20, n6_bit_full_adder_2_out_20, n6_bit_full_adder_3_out_20;

  _6_bit_Full_Adder u_6_bit_full_adder_1 (
    .in_2(in_2[0]), .in_3(in_2[1]), .in_4(in_2[2]), .in_5(in_2[3]), .in_6(in_2[4]), .in_7(in_2[5]),
    .in_8(in_3[0]), .in_9(in_3[1]), .in_10(in_3[2]), .in_11(in_3[3]), .in_12(in_3[4]), .in_13(in_3[5]),
    .in_1(in_1), .out_20(n6_bit_full_adder_1_out_20), .out_14(out_4[0]), .out_15(out_4[1]),
    .out_16(out_4[2]), .out_17(out_4[3]), .out_18(out_4[4]), .out_19(out_4[5]));
  _6_bit_Full_Adder u_6_bit_full_adder_2 (
    .in_2(in_2[6]), .in_3(in_2[7]), .in_4(in_2[8]), .in_5(in_2[9]), .in_6(in_2[10]), .in_7(in_2[11]),
    .in_8(in_3[6]), .in_9(in_3[7]), .in_10(in_3[8]), .in_11(in_3[9]), .in_12(in_3[10]), .in_13(in_3[11]),
    .in_1(n6_bit_full_adder_1_out_20), .out_20(n6_bit_full_adder_2_out_20), .out_14(out_4[6]),
    .out_15(out_4[7]), .out_16(out_4[8]), .out_17(out_4[9]), .out_18(out_4[10]), .out_19(out_4[11]));
  _6_bit_Full_Adder u_6_bit_full_adder_3 (
    .in_2(in_2[12]), .in_3(in_2[13]), .in_4(in_2[14]), .in_5(in_2[15]), .in_6(in_2[16]), .in_7(in_2[17]),
    .in_8(in_3[12]), .in_9(in_3[13]), .in_10(in_3[14]), .in_11(in_3[15]), .in_12(in_3[16]), .in_13(in_3[17]),
    .in_1(n6_bit_full_adder_2_out_20), .out_20(n6_bit_full_adder_3_out_20), .out_14(out_4[12]),
    .out_15(out_4[13]), .out_16(out_4[14]), .out_17(out_4[15]), .out_18(out_4[16]), .out_19(out_4[17]));
  Full_Adder full_adder_1 (
    .in_1(n6_bit_full_adder_3_out_20), .in_2(in_2[18]), .out_4(out_4[18]), .in_3(in_3[18]), .out_5(out_5));
endmodule

module _19_bit_XOR (
  input  in_1,
  input  [18:0] in_2,
  output [18:0] out_3
);

  wire [18:0] bit_extender_1_out;

  assign bit_extender_1_out = {{18{in_1}}, in_1};  // Bit_Extender bit_extender_1
  assign out_3 = bit_extender_1_out ^ in_2;  // XOR_Gate xor_1, 19 bits wide
endmodule

// 18TH
module _18th_bit_out (
  input  [18:0] in_1,
  output out_2
);


  assign out_2 = in_1[18];
endmodule

// AND
module _19_bit_AND (
  input  [18:0] A,
  input  [18:0] B,
  output [18:0] Result
);

  assign Result = A & B;  // AND_Gate and_1, 19 bits wide
endmodule

// OR
module _19_bit_OR (
  input  [18:0] A,
  input  [18:0] B,
  output [18:0] Result
);

  assign Result = A | B;  // OR_Gate or_1, 19 bits wide
endmodule

// add-SUB
module Add_Sub_circuit (
  input  SUB,
  input  [18:0] A,
  input  [18:0] B,
  output [18:0] S,
  output Co,
  output Overflow
);

  wire and_1_out, and_2_out, n18th_bit_out_1_out_2, n18th_bit_out_2_out_2, n18th_bit_out_3_out_2, not_1_out,
       not_2_out, not_3_out;
  wire [18:0] n19_bit_xor_1_out_3;

  _18th_bit_out u_18th_bit_out_1 (.in_1(A), .out_2(n18th_bit_out_1_out_2));
  not not_1 (not_1_out, n18th_bit_out_1_out_2);
  _19_bit_XOR u_19_bit_xor_1 (.in_1(SUB), .in_2(B), .out_3(n19_bit_xor_1_out_3));
  _19_bit_Full_Adder u_19_bit_full_adder_1 (.in_2(A), .in_3(n19_bit_xor_1_out_3), .in_1(SUB), .out_5(Co), .out_4(S));
  _18th_bit_out u_18th_bit_out_2 (.in_1(n19_bit_xor_1_out_3), .out_2(n18th_bit_out_2_out_2));
  not not_2 (not_2_out, n18th_bit_out_2_out_2);
  _18th_bit_out u_18th_bit_out_3 (.in_1(S), .out_2(n18th_bit_out_3_out_2));
  not not_3 (not_3_out, n18th_bit_out_3_out_2);
  and and_1 (and_1_out, not_3_out, n18th_bit_out_1_out_2, n18th_bit_out_2_out_2);
  and and_2 (and_2_out, n18th_bit_out_3_out_2, not_2_out, not_1_out);
  or or_1 (Overflow, and_1_out, and_2_out);
endmodule

// NOR
module _19_bit_Reduce_NOR (
  input  [18:0] in_1,
  output out_2
);

  nor nor_1 (out_2, in_1[0], in_1[1], in_1[2], in_1[3], in_1[4], in_1[5], in_1[6], in_1[7], in_1[8], in_1[9], in_1[10], in_1[11], in_1[12], in_1[13], in_1[14], in_1[15], in_1[16], in_1[17], in_1[18]);
endmodule
